// Logisim project MENOR QUE.circ as structural Verilog: 2 circuits, main circuit comparador
module comparador (
  input  [31:0] A,
  input  [31:0] B,
  output out_3
);

  wire [30:0] adder_1_out;
  wire [31:0] inverte_e_soma_um_1_out_2;

  inverte_e_soma_um inverte_e_soma_um_1 (.in_1(B), .out_2(inverte_e_soma_um_1_out_2));
  Adder #(.width(32)) adder_1 (.a(A), .b(inverte_e_soma_um_1_out_2), .out({out_3, adder_1_out}));  // open: cin, cout
endmodule

module inverte_e_soma_um (
  input  [31:0] in_1,
  output [31:0] out_2
);

  wire [31:0] not_1_out;

  assign not_1_out = ~in_1;  // NOT_Gate not_1, 32 bits wide
  Adder #(.width(32)) adder_1 (.a(not_1_out), .b(32'h1), .out(out_2));  // open: cin, cout
endmodule
