// Logisim project MULTIPLICADOR 32 BITS.circ as structural Verilog: 3 circuits, main circuit multvetorial32b
module multvetorial32b (
  input  [31:0] multiplicando,
  input  [31:0] Multiplicador,
  output [31:0] out_3
);

  wire bitfinder_1_found, bitfinder_2_found, bitfinder_3_found, bitfinder_4_found, bitfinder_5_found,
       bitfinder_6_found, bitfinder_7_found, bitfinder_8_found, bitfinder_9_found, bitfinder_10_found,
       bitfinder_11_found, bitfinder_12_found, bitfinder_13_found, bitfinder_14_found, bitfinder_15_found,
       bitfinder_16_found, bitfinder_17_found, bitfinder_18_found, bitfinder_19_found, bitfinder_20_found,
       bitfinder_21_found, bitfinder_22_found, bitfinder_23_found, bitfinder_24_found, bitfinder_25_found,
       bitfinder_26_found, bitfinder_27_found, bitfinder_28_found, bitfinder_29_found, bitfinder_30_found,
       bitfinder_31_found, bitfinder_32_found;
  wire [4:0] bitfinder_1_index, bitfinder_2_index, bitfinder_3_index, bitfinder_4_index, bitfinder_5_index,
       bitfinder_6_index, bitfinder_7_index, bitfinder_8_index, bitfinder_9_index, bitfinder_10_index,
       bitfinder_11_index, bitfinder_12_index, bitfinder_13_index, bitfinder_14_index, bitfinder_15_index,
       bitfinder_16_index, bitfinder_17_index, bitfinder_18_index, bitfinder_19_index, bitfinder_20_index,
       bitfinder_21_index, bitfinder_22_index, bitfinder_23_index, bitfinder_24_index, bitfinder_25_index,
       bitfinder_26_index, bitfinder_27_index, bitfinder_28_index, bitfinder_29_index, bitfinder_30_index,
       bitfinder_31_index, bitfinder_32_index;
  wire [31:0] adder_1_out, adder_2_out, adder_3_out, adder_4_out, adder_5_out, adder_6_out, adder_7_out,
       adder_8_out, adder_9_out, adder_10_out, adder_11_out, adder_12_out, adder_13_out, adder_14_out,
       adder_15_out, adder_16_out, adder_17_out, adder_18_out, adder_19_out, adder_20_out, adder_21_out,
       adder_22_out, adder_23_out, adder_24_out, adder_25_out, adder_26_out, adder_27_out, adder_28_out,
       adder_29_out, adder_30_out, deslocador_1_out_4, deslocador_2_out_4, deslocador_3_out_4,
       deslocador_4_out_4, deslocador_5_out_4, deslocador_6_out_4, deslocador_7_out_4, deslocador_8_out_4,
       deslocador_9_out_4, deslocador_10_out_4, deslocador_11_out_4, deslocador_12_out_4,
       deslocador_13_out_4, deslocador_14_out_4, deslocador_15_out_4, deslocador_16_out_4,
       deslocador_17_out_4, deslocador_18_out_4, deslocador_19_out_4, deslocador_20_out_4,
       deslocador_21_out_4, deslocador_22_out_4, deslocador_23_out_4, deslocador_24_out_4,
       deslocador_25_out_4, deslocador_26_out_4, deslocador_27_out_4, deslocador_28_out_4,
       deslocador_29_out_4, deslocador_30_out_4, deslocador_31_out_4, deslocador_32_out_4, extensor_1_out_2,
       extensor_1_out_3, extensor_1_out_4, extensor_1_out_5, extensor_1_out_6, extensor_1_out_7,
       extensor_1_out_8, extensor_1_out_9, extensor_1_out_10, extensor_1_out_11, extensor_1_out_12,
       extensor_1_out_13, extensor_1_out_14, extensor_1_out_15, extensor_1_out_16, extensor_1_out_17,
       extensor_1_out_18, extensor_1_out_19, extensor_1_out_20, extensor_1_out_21, extensor_1_out_22,
       extensor_1_out_23, extensor_1_out_24, extensor_1_out_25, extensor_1_out_26, extensor_1_out_27,
       extensor_1_out_28, extensor_1_out_29, extensor_1_out_30, extensor_1_out_31, extensor_1_out_32,
       extensor_1_out_33;

  extensor extensor_1 (
    .in_1(Multiplicador), .out_2(extensor_1_out_2), .out_3(extensor_1_out_3), .out_4(extensor_1_out_4),
    .out_5(extensor_1_out_5), .out_6(extensor_1_out_6), .out_7(extensor_1_out_7), .out_8(extensor_1_out_8),
    .out_9(extensor_1_out_9), .out_10(extensor_1_out_10), .out_11(extensor_1_out_11),
    .out_12(extensor_1_out_12), .out_13(extensor_1_out_13), .out_14(extensor_1_out_14),
    .out_15(extensor_1_out_15), .out_16(extensor_1_out_16), .out_17(extensor_1_out_17),
    .out_18(extensor_1_out_18), .out_19(extensor_1_out_19), .out_20(extensor_1_out_20),
    .out_21(extensor_1_out_21), .out_22(extensor_1_out_22), .out_23(extensor_1_out_23),
    .out_24(extensor_1_out_24), .out_25(extensor_1_out_25), .out_26(extensor_1_out_26),
    .out_27(extensor_1_out_27), .out_28(extensor_1_out_28), .out_29(extensor_1_out_29),
    .out_30(extensor_1_out_30), .out_31(extensor_1_out_31), .out_32(extensor_1_out_32),
    .out_33(extensor_1_out_33));
  BitFinder #(.width(32)) bitfinder_1 (.in(extensor_1_out_2), .index(bitfinder_1_index), .found(bitfinder_1_found));
  BitFinder #(.width(32)) bitfinder_2 (.in(extensor_1_out_3), .index(bitfinder_2_index), .found(bitfinder_2_found));
  BitFinder #(.width(32)) bitfinder_3 (.in(extensor_1_out_4), .index(bitfinder_3_index), .found(bitfinder_3_found));
  BitFinder #(.width(32)) bitfinder_4 (.in(extensor_1_out_5), .index(bitfinder_4_index), .found(bitfinder_4_found));
  BitFinder #(.width(32)) bitfinder_5 (.in(extensor_1_out_6), .index(bitfinder_5_index), .found(bitfinder_5_found));
  BitFinder #(.width(32)) bitfinder_6 (.in(extensor_1_out_7), .index(bitfinder_6_index), .found(bitfinder_6_found));
  BitFinder #(.width(32)) bitfinder_7 (.in(extensor_1_out_8), .index(bitfinder_7_index), .found(bitfinder_7_found));
  BitFinder #(.width(32)) bitfinder_8 (.in(extensor_1_out_9), .index(bitfinder_8_index), .found(bitfinder_8_found));
  BitFinder #(.width(32)) bitfinder_9 (.in(extensor_1_out_10), .index(bitfinder_9_index), .found(bitfinder_9_found));
  BitFinder #(.width(32)) bitfinder_10 (.in(extensor_1_out_11), .index(bitfinder_10_index), .found(bitfinder_10_found));
  BitFinder #(.width(32)) bitfinder_11 (.in(extensor_1_out_12), .index(bitfinder_11_index), .found(bitfinder_11_found));
  BitFinder #(.width(32)) bitfinder_12 (.in(extensor_1_out_13), .index(bitfinder_12_index), .found(bitfinder_12_found));
  BitFinder #(.width(32)) bitfinder_13 (.in(extensor_1_out_14), .index(bitfinder_13_index), .found(bitfinder_13_found));
  BitFinder #(.width(32)) bitfinder_14 (.in(extensor_1_out_15), .index(bitfinder_14_index), .found(bitfinder_14_found));
  BitFinder #(.width(32)) bitfinder_15 (.in(extensor_1_out_16), .index(bitfinder_15_index), .found(bitfinder_15_found));
  BitFinder #(.width(32)) bitfinder_16 (.in(extensor_1_out_17), .index(bitfinder_16_index), .found(bitfinder_16_found));
  BitFinder #(.width(32)) bitfinder_17 (.in(extensor_1_out_18), .index(bitfinder_17_index), .found(bitfinder_17_found));
  BitFinder #(.width(32)) bitfinder_18 (.in(extensor_1_out_19), .index(bitfinder_18_index), .found(bitfinder_18_found));
  BitFinder #(.width(32)) bitfinder_19 (.in(extensor_1_out_20), .index(bitfinder_19_index), .found(bitfinder_19_found));
  BitFinder #(.width(32)) bitfinder_20 (.in(extensor_1_out_21), .index(bitfinder_20_index), .found(bitfinder_20_found));
  BitFinder #(.width(32)) bitfinder_21 (.in(extensor_1_out_22), .index(bitfinder_21_index), .found(bitfinder_21_found));
  BitFinder #(.width(32)) bitfinder_22 (.in(extensor_1_out_23), .index(bitfinder_22_index), .found(bitfinder_22_found));
  BitFinder #(.width(32)) bitfinder_23 (.in(extensor_1_out_24), .index(bitfinder_23_index), .found(bitfinder_23_found));
  BitFinder #(.width(32)) bitfinder_24 (.in(extensor_1_out_25), .index(bitfinder_24_index), .found(bitfinder_24_found));
  BitFinder #(.width(32)) bitfinder_25 (.in(extensor_1_out_26), .index(bitfinder_25_index), .found(bitfinder_25_found));
  BitFinder #(.width(32)) bitfinder_26 (.in(extensor_1_out_27), .index(bitfinder_26_index), .found(bitfinder_26_found));
  BitFinder #(.width(32)) bitfinder_27 (.in(extensor_1_out_28), .index(bitfinder_27_index), .found(bitfinder_27_found));
  BitFinder #(.width(32)) bitfinder_28 (.in(extensor_1_out_29), .index(bitfinder_28_index), .found(bitfinder_28_found));
  BitFinder #(.width(32)) bitfinder_29 (.in(extensor_1_out_30), .index(bitfinder_29_index), .found(bitfinder_29_found));
  BitFinder #(.width(32)) bitfinder_30 (.in(extensor_1_out_31), .index(bitfinder_30_index), .found(bitfinder_30_found));
  BitFinder #(.width(32)) bitfinder_31 (.in(extensor_1_out_32), .index(bitfinder_31_index), .found(bitfinder_31_found));
  BitFinder #(.width(32)) bitfinder_32 (.in(extensor_1_out_33), .index(bitfinder_32_index), .found(bitfinder_32_found));
  deslocador deslocador_1 (
    .in_1(multiplicando), .in_2(bitfinder_1_index), .in_3(bitfinder_1_found), .out_4(deslocador_1_out_4));
  deslocador deslocador_2 (
    .in_1(multiplicando), .in_2(bitfinder_2_index), .in_3(bitfinder_2_found), .out_4(deslocador_2_out_4));
  deslocador deslocador_3 (
    .in_1(multiplicando), .in_2(bitfinder_3_index), .in_3(bitfinder_3_found), .out_4(deslocador_3_out_4));
  deslocador deslocador_4 (
    .in_1(multiplicando), .in_2(bitfinder_4_index), .in_3(bitfinder_4_found), .out_4(deslocador_4_out_4));
  deslocador deslocador_5 (
    .in_1(multiplicando), .in_2(bitfinder_5_index), .in_3(bitfinder_5_found), .out_4(deslocador_5_out_4));
  deslocador deslocador_6 (
    .in_1(multiplicando), .in_2(bitfinder_6_index), .in_3(bitfinder_6_found), .out_4(deslocador_6_out_4));
  deslocador deslocador_7 (
    .in_1(multiplicando), .in_2(bitfinder_7_index), .in_3(bitfinder_7_found), .out_4(deslocador_7_out_4));
  deslocador deslocador_8 (
    .in_1(multiplicando), .in_2(bitfinder_8_index), .in_3(bitfinder_8_found), .out_4(deslocador_8_out_4));
  deslocador deslocador_9 (
    .in_1(multiplicando), .in_2(bitfinder_9_index), .in_3(bitfinder_9_found), .out_4(deslocador_9_out_4));
  deslocador deslocador_10 (
    .in_1(multiplicando), .in_2(bitfinder_10_index), .in_3(bitfinder_10_found), .out_4(deslocador_10_out_4));
  deslocador deslocador_11 (
    .in_1(multiplicando), .in_2(bitfinder_11_index), .in_3(bitfinder_11_found), .out_4(deslocador_11_out_4));
  deslocador deslocador_12 (
    .in_1(multiplicando), .in_2(bitfinder_12_index), .in_3(bitfinder_12_found), .out_4(deslocador_12_out_4));
  deslocador deslocador_13 (
    .in_1(multiplicando), .in_2(bitfinder_13_index), .in_3(bitfinder_13_found), .out_4(deslocador_13_out_4));
  deslocador deslocador_14 (
    .in_1(multiplicando), .in_2(bitfinder_14_index), .in_3(bitfinder_14_found), .out_4(deslocador_14_out_4));
  deslocador deslocador_15 (
    .in_1(multiplicando), .in_2(bitfinder_15_index), .in_3(bitfinder_15_found), .out_4(deslocador_15_out_4));
  deslocador deslocador_16 (
    .in_1(multiplicando), .in_2(bitfinder_16_index), .in_3(bitfinder_16_found), .out_4(deslocador_16_out_4));
  deslocador deslocador_17 (
    .in_1(multiplicando), .in_2(bitfinder_17_index), .in_3(bitfinder_17_found), .out_4(deslocador_17_out_4));
  deslocador deslocador_18 (
    .in_1(multiplicando), .in_2(bitfinder_18_index), .in_3(bitfinder_18_found), .out_4(deslocador_18_out_4));
  deslocador deslocador_19 (
    .in_1(multiplicando), .in_2(bitfinder_19_index), .in_3(bitfinder_19_found), .out_4(deslocador_19_out_4));
  deslocador deslocador_20 (
    .in_1(multiplicando), .in_2(bitfinder_20_index), .in_3(bitfinder_20_found), .out_4(deslocador_20_out_4));
  deslocador deslocador_21 (
    .in_1(multiplicando), .in_2(bitfinder_21_index), .in_3(bitfinder_21_found), .out_4(deslocador_21_out_4));
  deslocador deslocador_22 (
    .in_1(multiplicando), .in_2(bitfinder_22_index), .in_3(bitfinder_22_found), .out_4(deslocador_22_out_4));
  deslocador deslocador_23 (
    .in_1(multiplicando), .in_2(bitfinder_23_index), .in_3(bitfinder_23_found), .out_4(deslocador_23_out_4));
  deslocador deslocador_24 (
    .in_1(multiplicando), .in_2(bitfinder_24_index), .in_3(bitfinder_24_found), .out_4(deslocador_24_out_4));
  deslocador deslocador_25 (
    .in_1(multiplicando), .in_2(bitfinder_25_index), .in_3(bitfinder_25_found), .out_4(deslocador_25_out_4));
  deslocador deslocador_26 (
    .in_1(multiplicando), .in_2(bitfinder_26_index), .in_3(bitfinder_26_found), .out_4(deslocador_26_out_4));
  deslocador deslocador_27 (
    .in_1(multiplicando), .in_2(bitfinder_27_index), .in_3(bitfinder_27_found), .out_4(deslocador_27_out_4));
  deslocador deslocador_28 (
    .in_1(multiplicando), .in_2(bitfinder_28_index), .in_3(bitfinder_28_found), .out_4(deslocador_28_out_4));
  deslocador deslocador_29 (
    .in_1(multiplicando), .in_2(bitfinder_29_index), .in_3(bitfinder_29_found), .out_4(deslocador_29_out_4));
  deslocador deslocador_30 (
    .in_1(multiplicando), .in_2(bitfinder_30_index), .in_3(bitfinder_30_found), .out_4(deslocador_30_out_4));
  deslocador deslocador_31 (
    .in_1(multiplicando), .in_2(bitfinder_31_index), .in_3(bitfinder_31_found), .out_4(deslocador_31_out_4));
  deslocador deslocador_32 (
    .in_1(multiplicando), .in_2(bitfinder_32_index), .in_3(bitfinder_32_found), .out_4(deslocador_32_out_4));
  Adder #(.width(32)) adder_1 (.a(deslocador_1_out_4), .b(deslocador_2_out_4), .out(adder_1_out));  // open: cin, cout
  Adder #(.width(32)) adder_2 (.a(deslocador_3_out_4), .b(deslocador_4_out_4), .out(adder_2_out));  // open: cin, cout
  Adder #(.width(32)) adder_3 (.a(deslocador_5_out_4), .b(deslocador_6_out_4), .out(adder_3_out));  // open: cin, cout
  Adder #(.width(32)) adder_4 (.a(deslocador_7_out_4), .b(deslocador_8_out_4), .out(adder_4_out));  // open: cin, cout
  Adder #(.width(32)) adder_5 (.a(deslocador_9_out_4), .b(deslocador_10_out_4), .out(adder_5_out));  // open: cin, cout
  Adder #(.width(32)) adder_6 (.a(deslocador_11_out_4), .b(deslocador_12_out_4), .out(adder_6_out));  // open: cin, cout
  Adder #(.width(32)) adder_7 (.a(deslocador_13_out_4), .b(deslocador_14_out_4), .out(adder_7_out));  // open: cin, cout
  Adder #(.width(32)) adder_8 (.a(deslocador_15_out_4), .b(deslocador_16_out_4), .out(adder_8_out));  // open: cin, cout
  Adder #(.width(32)) adder_9 (.a(deslocador_17_out_4), .b(deslocador_18_out_4), .out(adder_9_out));  // open: cin, cout
  Adder #(.width(32)) adder_10 (
    .a(deslocador_19_out_4), .b(deslocador_20_out_4), .out(adder_10_out));  // open: cin, cout
  Adder #(.width(32)) adder_11 (
    .a(deslocador_21_out_4), .b(deslocador_22_out_4), .out(adder_11_out));  // open: cin, cout
  Adder #(.width(32)) adder_12 (
    .a(deslocador_23_out_4), .b(deslocador_24_out_4), .out(adder_12_out));  // open: cin, cout
  Adder #(.width(32)) adder_13 (
    .a(deslocador_25_out_4), .b(deslocador_26_out_4), .out(adder_13_out));  // open: cin, cout
  Adder #(.width(32)) adder_14 (
    .a(deslocador_27_out_4), .b(deslocador_28_out_4), .out(adder_14_out));  // open: cin, cout
  Adder #(.width(32)) adder_15 (
    .a(deslocador_29_out_4), .b(deslocador_30_out_4), .out(adder_15_out));  // open: cin, cout
  Adder #(.width(32)) adder_16 (
    .a(deslocador_31_out_4), .b(deslocador_32_out_4), .out(adder_16_out));  // open: cin, cout
  Adder #(.width(32)) adder_17 (.a(adder_1_out), .b(adder_2_out), .out(adder_17_out));  // open: cin, cout
  Adder #(.width(32)) adder_18 (.a(adder_3_out), .b(adder_4_out), .out(adder_18_out));  // open: cin, cout
  Adder #(.width(32)) adder_19 (.a(adder_5_out), .b(adder_6_out), .out(adder_19_out));  // open: cin, cout
  Adder #(.width(32)) adder_20 (.a(adder_7_out), .b(adder_8_out), .out(adder_20_out));  // open: cin, cout
  Adder #(.width(32)) adder_21 (.a(adder_9_out), .b(adder_10_out), .out(adder_21_out));  // open: cin, cout
  Adder #(.width(32)) adder_22 (.a(adder_11_out), .b(adder_12_out), .out(adder_22_out));  // open: cin, cout
  Adder #(.width(32)) adder_23 (.a(adder_13_out), .b(adder_14_out), .out(adder_23_out));  // open: cin, cout
  Adder #(.width(32)) adder_24 (.a(adder_15_out), .b(adder_16_out), .out(adder_24_out));  // open: cin, cout
  Adder #(.width(32)) adder_25 (.a(adder_19_out), .b(adder_20_out), .out(adder_25_out));  // open: cin, cout
  Adder #(.width(32)) adder_26 (.a(adder_21_out), .b(adder_22_out), .out(adder_26_out));  // open: cin, cout
  Adder #(.width(32)) adder_27 (.a(adder_23_out), .b(adder_24_out), .out(adder_27_out));  // open: cin, cout
  Adder #(.width(32)) adder_28 (.a(adder_17_out), .b(adder_18_out), .out(adder_28_out));  // open: cin, cout
  Adder #(.width(32)) adder_29 (.a(adder_28_out), .b(adder_25_out), .out(adder_29_out));  // open: cin, cout
  Adder #(.width(32)) adder_30 (.a(adder_26_out), .b(adder_27_out), .out(adder_30_out));  // open: cin, cout
  Adder #(.width(32)) adder_31 (.a(adder_29_out), .b(adder_30_out), .out(out_3));  // open: cin, cout
endmodule

module extensor (
  input  [31:0] in_1,
  output [31:0] out_2,
  output [31:0] out_3,
  output [31:0] out_4,
  output [31:0] out_5,
  output [31:0] out_6,
  output [31:0] out_7,
  output [31:0] out_8,
  output [31:0] out_9,
  output [31:0] out_10,
  output [31:0] out_11,
  output [31:0] out_12,
  output [31:0] out_13,
  output [31:0] out_14,
  output [31:0] out_15,
  output [31:0] out_16,
  output [31:0] out_17,
  output [31:0] out_18,
  output [31:0] out_19,
  output [31:0] out_20,
  output [31:0] out_21,
  output [31:0] out_22,
  output [31:0] out_23,
  output [31:0] out_24,
  output [31:0] out_25,
  output [31:0] out_26,
  output [31:0] out_27,
  output [31:0] out_28,
  output [31:0] out_29,
  output [31:0] out_30,
  output [31:0] out_31,
  output [31:0] out_32,
  output [31:0] out_33
);

  assign out_2 = in_1 & 32'h80000000;  // AND_Gate and_1, 32 bits wide
  assign out_3 = in_1 & 32'h40000000;  // AND_Gate and_2, 32 bits wide
  assign out_4 = in_1 & 32'h20000000;  // AND_Gate and_3, 32 bits wide
  assign out_5 = in_1 & 32'h10000000;  // AND_Gate and_4, 32 bits wide
  assign out_6 = in_1 & 32'h8000000;  // AND_Gate and_5, 32 bits wide
  assign out_7 = in_1 & 32'h4000000;  // AND_Gate and_6, 32 bits wide
  assign out_8 = in_1 & 32'h2000000;  // AND_Gate and_7, 32 bits wide
  assign out_9 = in_1 & 32'h1000000;  // AND_Gate and_8, 32 bits wide
  assign out_10 = in_1 & 32'h800000;  // AND_Gate and_9, 32 bits wide
  assign out_11 = in_1 & 32'h400000;  // AND_Gate and_10, 32 bits wide
  assign out_12 = in_1 & 32'h200000;  // AND_Gate and_11, 32 bits wide
  assign out_13 = in_1 & 32'h100000;  // AND_Gate and_12, 32 bits wide
  assign out_14 = in_1 & 32'h80000;  // AND_Gate and_13, 32 bits wide
  assign out_15 = in_1 & 32'h40000;  // AND_Gate and_14, 32 bits wide
  assign out_16 = in_1 & 32'h20000;  // AND_Gate and_15, 32 bits wide
  assign out_17 = in_1 & 32'h10000;  // AND_Gate and_16, 32 bits wide
  assign out_18 = in_1 & 32'h8000;  // AND_Gate and_17, 32 bits wide
  assign out_19 = in_1 & 32'h4000;  // AND_Gate and_18, 32 bits wide
  assign out_20 = in_1 & 32'h2000;  // AND_Gate and_19, 32 bits wide
  assign out_21 = in_1 & 32'h1000;  // AND_Gate and_20, 32 bits wide
  assign out_22 = in_1 & 32'h800;  // AND_Gate and_21, 32 bits wide
  assign out_23 = in_1 & 32'h400;  // AND_Gate and_22, 32 bits wide
  assign out_24 = in_1 & 32'h200;  // AND_Gate and_23, 32 bits wide
  assign out_25 = in_1 & 32'h100;  // AND_Gate and_24, 32 bits wide
  assign out_26 = in_1 & 32'h80;  // AND_Gate and_25, 32 bits wide
  assign out_27 = in_1 & 32'h40;  // AND_Gate and_26, 32 bits wide
  assign out_28 = in_1 & 32'h20;  // AND_Gate and_27, 32 bits wide
  assign out_29 = in_1 & 32'h10;  // AND_Gate and_28, 32 bits wide
  assign out_30 = in_1 & 32'h8;  // AND_Gate and_29, 32 bits wide
  assign out_31 = in_1 & 32'h4;  // AND_Gate and_30, 32 bits wide
  assign out_32 = in_1 & 32'h2;  // AND_Gate and_31, 32 bits wide
  assign out_33 = in_1 & 32'h1;  // AND_Gate and_32, 32 bits wide
endmodule

module deslocador (
  input  [31:0] in_1,
  input  [4:0] in_2,
  input  in_3,
  output [31:0] out_4
);

  wire not_1_out;
  wire [31:0] shifter_1_out;

  Shifter #(.width(32)) shifter_1 (.in(in_1), .\dist (in_2), .out(shifter_1_out));
  not not_1 (not_1_out, in_3);
  Multiplexer #(.width(32), .enable("false")) multiplexer_1 (
    .in0(shifter_1_out), .in1({32{1'b0}}), .out(out_4), .sel(not_1_out));
endmodule
